# Fritzing sketch Circuit_LedFull3D7Seg_BTColor (saved by Fritzing 0.9.3b)
breadboards: 1

parts:
  Part1 = Arduino Nano (Rev3.0)
  DS1 = DS18B20 1-Wire Temperature Sensor [part_number=DS18B20]
  R1 = Resistor [tolerance=±5% resistance=4.7k package="0603 [SMD]"]
  LED_full_1903 = Header 3 [package=molex-1x3_lock]
  Part2 = Bluetooth HC-05 Macho
  R2 = Resistor [tolerance=±5% resistance=660 package="0603 [SMD]"]
  R3 = Resistor [tolerance=±5% resistance=330 package="0603 [SMD]"]

nets:
  GND: Part1.GND, DS1.GND, LED_full_1903.1, Part2.GND, R2.Pin_0
  N1: Part1.D2, DS1.DQ, R1.Pin_1
  N2: Part1.D3, LED_full_1903.2
  N3: Part1.D4, Part2.TXD
  N4: Part1.D5, R3.Pin_0
  VIN: Part1.VIN, DS1.VDD, R1.Pin_0, LED_full_1903.3, Part2.VCC
  N5: Part2.RXD, R2.Pin_1, R3.Pin_1
